// Logisim project alu.circ as structural Verilog: 1 circuit, main circuit alu
module alu (
  input  [5:0] ALU_OP,
  input  [7:0] A,
  input  [7:0] B,
  input  OE_n,
  input  RST_n,
  input  WE_n,
  input  CLK,
  output [7:0] DataBusOut,
  output A_equal_B,
  output ZERO
);

  wire and_1_out, ic74181_1_p7, ic74181_1_p8, ic74181_2_p7, nor_1_out, or_1_out;
  wire [3:0] ic74181_1_p6, ic74181_2_p6;

  or or_1 (or_1_out, WE_n, CLK);
  // IC74181 ic74181_1: pin names not known; wires that end beside it: ALU_OP[3:0], ALU_OP[4], A[3:0], B[3:0], ALU_OP[5], ic74181_1_p6, ic74181_1_p7, ic74181_1_p8
  // IC74181 ic74181_2: pin names not known; wires that end beside it: ALU_OP[3:0], ALU_OP[4], A[7:4], B[7:4], ic74181_1_p8, ic74181_2_p6, ic74181_2_p7
  and and_1 (and_1_out, ic74181_1_p7, ic74181_2_p7);
  // IC_74245 ic_74245_1: pin names not known; wires that end beside it: OE_n
  nor nor_1 (nor_1_out, ic74181_1_p6[0], ic74181_1_p6[1], ic74181_1_p6[2], ic74181_1_p6[3], ic74181_2_p6[0], ic74181_2_p6[1], ic74181_2_p6[2], ic74181_2_p6[3]);
  // IC_74273 ic_74273_1: pin names not known; wires that end beside it: and_1_out, nor_1_out, or_1_out, RST_n, A_equal_B, ZERO
endmodule
