// Logisim project immediate_register.circ as structural Verilog: 1 circuit, main circuit immediate_register
module immediate_register (
  input  [7:0] DataBusIn,
  input  WE_L_n,
  input  WE_H_n,
  input  ADDR_OE_n,
  input  CLK,
  output [7:0] ALU_OP,
  output [15:0] AddrBusOut
);

  // IC_74377 LOW: pin names not known
  // IC_74377 ic_74377_1: pin names not known; wires that end beside it: CLK, WE_L_n, CLK, WE_H_n
  // IC_74245 ic_74245_1: pin names not known
  // IC_74245 ic_74245_2: pin names not known; wires that end beside it: ADDR_OE_n, ADDR_OE_n
endmodule
