// Logisim project instruction_register.circ as structural Verilog: 1 circuit, main circuit instruction_register
module instruction_register (
  input  [7:0] DataBusIn,
  input  WE_n,
  input  RST_n,
  input  CLK,
  output [7:0] INSTRUCTION
);

  wire nor_1_out;

  nor nor_1 (nor_1_out, CLK, WE_n);
  // IC_74273 ic_74273_1: pin names not known; wires that end beside it: nor_1_out, RST_n
endmodule
