// Logisim project interrupt_handler.circ as structural Verilog: 1 circuit, main circuit interrupt_handler
module interrupt_handler (
  input  IRQ_0_n,
  input  IRQ_1_n,
  input  IRQ_2_n,
  input  IRQ_3_n,
  input  IRQ_4_n,
  input  IRQ_5_n,
  input  IRQ_6_n,
  input  IRQ_7_n,
  input  IRQ_MASK,
  input  IRQ_ADDR_OE_n,
  output [15:0] IRQ_ADDR,
  output INTERRUPT_n
);

  wire [2:0] ic74148_1_p10, not_1_out;

  // IC74148 ic74148_1: pin names not known; wires that end beside it: IRQ_0_n, IRQ_1_n, IRQ_2_n, IRQ_3_n, IRQ_4_n, IRQ_5_n, IRQ_6_n, IRQ_7_n, IRQ_MASK, ic74148_1_p10, INTERRUPT_n
  assign not_1_out = ~ic74148_1_p10;  // NOT_Gate not_1, 3 bits wide
  // IC_74245 ic_74245_1: pin names not known
  // IC_74245 ic_74245_2: pin names not known; wires that end beside it: IRQ_ADDR_OE_n, IRQ_ADDR_OE_n

  // Notes on the sheet:
  //   top 2 bits = 01 (16KiB range between RAM and ROM)
  //   next 3 bits = IRQ address, IRQ0=000, IRQ7=111
  //   bottom 11 bits = 2KiB addr. space per device
endmodule
