// Logisim project ata_port.circ as structural Verilog: 2 circuits, main circuit main
module main (
  input  [15:0] ADDR_BUS,
  input  n_WRAM,
  input  [3:0] SEQ,
  input  [7:0] DATA_BUS_IN,
  input  [15:0] ATA_DATA_READ,
  output [2:0] ATA_ADDR,
  output n_ATA_CS0,
  output n_ATA_CS1,
  output n_ATA_RD,
  output n_ATA_WR,
  output [15:0] ATA_DATA_WRITE,
  output [7:0] DATA_BUS_OUT
);

  wire ADDR_C3, ADDR_C3_buf, and_1_out, and_2_out, CLK, n74377_1_pin1, n_ADDR_C3, n_ADDR_C3_buf, n_ATAHI,
       n_CLK, n_CS0gen, n_CS1gen, n_HIRD, n_HIWR, n_RDgen, n_WRgen, nand_5_out, not_1_out, not_4_out,
       not_5_out, not_6_out, not_7_out, SEQ45, WRAM;
  wire [7:0] HIDATA_fromATA_q, HIDATA_toATA_q;

  not not_1 (not_1_out, ADDR_BUS[3]);
  Register #(.trigger("high"), .width(3)) register_1 (
    .D(ADDR_BUS[2:0]), .en(1'b1), .clk(n_ADDR_C3_buf), .Q(ATA_ADDR), .clr(1'b0));
  nand nand_1 (n_CS0gen, not_1_out, ADDR_C3);
  nand nand_2 (n_CS1gen, ADDR_C3, ADDR_BUS[3]);
  _74377 u_74377_1 (
    .pin1(n74377_1_pin1), .pin6(n_ADDR_C3_buf), .pin7(n_ADDR_C3), .pin8(n_WRgen), .pin9(n_ATA_WR),
    .pin19(n_ATA_CS0), .pin18(n_CS0gen), .pin17(n_CS1gen), .pin16(n_ATA_CS1), .pin15(ADDR_C3_buf),
    .pin14(ADDR_C3), .pin13(n_RDgen), .pin12(n_ATA_RD), .pin11(n_CLK));  // open: pin2, pin3, pin4, pin5
  // Probe on ATA_ADDR
  nor nor_1 (ADDR_C3, ~ADDR_BUS[15], ~ADDR_BUS[14], ADDR_BUS[13], ADDR_BUS[12], ADDR_BUS[11], ADDR_BUS[10], ~ADDR_BUS[9], ~ADDR_BUS[8]);  // NOR_Gate
  Clock u_CLK (.out(CLK));
  not not_2 (n_ADDR_C3, ADDR_C3);
  not not_3 (n_CLK, CLK);
  and and_1 (and_1_out, ADDR_C3, ADDR_BUS[4]);
  nor nor_2 (SEQ45, 1'b0, SEQ[1], ~SEQ[2], SEQ[3]);  // NOR_Gate
  nand nand_3 (n_HIWR, and_1_out, WRAM);
  nand nand_4 (n_HIRD, and_1_out, n_WRAM);
  Register HIDATA_toATA (.D(DATA_BUS_IN), .en(not_4_out), .clk(CLK), .Q(HIDATA_toATA_q));  // open: clr
  not not_4 (not_4_out, n_HIWR);
  Register HIDATA_fromATA (.D(ATA_DATA_READ[15:8]), .en(not_5_out), .clk(CLK), .Q(HIDATA_fromATA_q));  // open: clr
  not not_5 (not_5_out, n_ATA_RD);
  assign ATA_DATA_WRITE[15:8] = not_6_out ? HIDATA_toATA_q : 8'bz;  // Controlled_Buffer controlled_buffer_1
  not not_6 (not_6_out, n_ATAHI);
  assign DATA_BUS_OUT = not_7_out ? HIDATA_fromATA_q : 8'bz;  // Controlled_Buffer controlled_buffer_2
  not not_7 (not_7_out, n_HIRD);
  nand nand_5 (nand_5_out, n_ATA_CS0, n_ATA_CS1);
  assign DATA_BUS_OUT = nand_5_out ? ATA_DATA_READ[7:0] : 8'bz;  // Controlled_Buffer controlled_buffer_3
  not not_8 (WRAM, n_WRAM);
  nand nand_6 (n_ATAHI, ADDR_C3_buf, n_ATA_RD);
  and and_2 (and_2_out, ADDR_C3_buf, SEQ45);
  nand nand_7 (n_WRgen, and_2_out, WRAM);
  nand nand_8 (n_RDgen, and_2_out, n_WRAM);

  assign ATA_DATA_WRITE[7:0] = DATA_BUS_IN;
  // also tied to GND on the sheet: n74377_1_pin1

  // Other names for the same wires on the sheet: A0_2_buf[2:0] = ATA_ADDR; A0_2[2:0] = ADDR_BUS[2:0];
  //   A3 = ADDR_BUS[3]; A4 = ADDR_BUS[4]; n_CS0 = n_ATA_CS0; n_CS1 = n_ATA_CS1; n_RD = n_ATA_RD; n_WR = n_ATA_WR

  // Notes on the sheet:
  //   ADDR_BUS: initial=0xffff
  //   SEQ: initial=0x1
  //   n_WRAM: initial=0x1
  //   /WRAM only during sequence 0x5
  //   Assumes read and write operations that hold the address
  //   and/or data bus stable across sequences 0x4-0x6, and assert
  //   Group C G-J
  //   Simulate '245
  //   Simulate '245
  //   Do not implement
endmodule

module ata_port (
  input  D8,
  input  D9,
  input  D10,
  input  D11,
  input  D12,
  input  D13,
  input  D14,
  input  D15,
  input  PDIAG,
  input  A2,
  input  n_CS1,
  input  D7,
  input  D6,
  input  D5,
  input  D4,
  input  D3,
  input  D2,
  input  D1,
  input  D0,
  input  DMARQ,
  input  IORDY,
  input  IRQ,
  input  A1,
  input  A0,
  input  n_CS0,
  input  DASP,
  output GND2,
  output GND3,
  output GND4,
  output GND5,
  output CSEL,
  output GND6,
  output GND7,
  output n_RST,
  output GND1,
  output n_WR,
  output n_RD,
  output DMACK
);


  assign CSEL = 1'b0;
  assign DMACK = 1'b1;
  assign GND1 = 1'b0;
  assign GND2 = 1'b0;
  assign GND3 = 1'b0;
  assign GND4 = 1'b0;
  assign GND5 = 1'b0;
  assign GND6 = 1'b0;
  assign GND7 = 1'b0;

  // Other names for the same wires on the sheet: CPU_RST = n_RST
endmodule
