// Logisim project cd_regs.circ as structural Verilog: 1 circuit, main circuit main
module main (
  input  [3:0] CDSEL
);

  wire and_1_out, and_2_out, ic_74138_1_p7, ic_74138_1_p8, ic_74138_1_p9, ic_74138_1_p10, ic_74138_1_p11,
       ic_74138_2_p7, ic_74138_2_p8, ic_74138_2_p9, ic_74138_2_p10, ic_74138_2_p11, nor_1_out;

  nor nor_1 (nor_1_out, CDSEL[2], CDSEL[1], CDSEL[0], 1'b0);
  // IC_74138 ic_74138_1: pin names not known; wires that end beside it: CDSEL[0], CDSEL[1], CDSEL[2], nor_1_out, CDSEL[3], 1'b1, ic_74138_1_p7, ic_74138_1_p8, ic_74138_1_p9, ic_74138_1_p10, ic_74138_1_p11
  // IC_74138 ic_74138_2: pin names not known; wires that end beside it: CDSEL[0], CDSEL[1], CDSEL[2], nor_1_out, 1'b0, CDSEL[3], ic_74138_2_p7, ic_74138_2_p8, ic_74138_2_p9, ic_74138_2_p10, ic_74138_2_p11
  and and_1 (and_1_out, ic_74138_1_p9, ic_74138_1_p10);
  and and_2 (and_2_out, ic_74138_2_p9, ic_74138_2_p10);
  LED n_LOAD_CL (.in(ic_74138_1_p7));
  LED n_LOAD_CH (.in(ic_74138_1_p8));
  LED n_UP_DOWN_C (.in(ic_74138_1_p9));
  LED n_CTEN_C (.in(and_1_out));
  LED n_ADDR_C (.in(ic_74138_1_p11));
  LED n_LOAD_DL (.in(ic_74138_2_p7));
  LED n_LOAD_DH (.in(ic_74138_2_p8));
  LED n_UP_DOWN_D (.in(ic_74138_2_p9));
  LED n_CTEN_D (.in(and_2_out));
  LED n_ADDR_D (.in(ic_74138_2_p11));

  // Notes on the sheet:
  //   NOR output to /G2A
  //   CDSEL3 to /G2B for C
  //   CDSEL3 to G1 for D
endmodule
