// Logisim project expanded_ram_decode.circ as structural Verilog: 1 circuit, main circuit main
module main (
  input  [15:0] ADDR,
  input  nWRAM,
  output nCE,
  output A12,
  output nOE,
  output nWE
);

  wire clock_1_out, nand_1_out, nand_2_out, nand_3_out, nand_4_out, nor_1_out, not_1_out, not_2_out,
       not_3_out, not_4_out, not_5_out, not_6_out, not_7_out, not_8_out;

  Clock clock_1 (.out(clock_1_out));
  not not_1 (not_1_out, nWRAM);
  not not_2 (not_2_out, clock_1_out);
  not not_3 (not_3_out, ADDR[13]);
  not not_4 (not_4_out, ADDR[12]);
  not not_5 (not_5_out, ADDR[11]);
  nand nand_1 (nand_1_out, ADDR[15], ADDR[14], ADDR[13], ADDR[12]);
  nand nand_2 (nand_2_out, ADDR[11], ADDR[10], ADDR[9], ADDR[8], ADDR[7], ADDR[6], ADDR[5], ADDR[4]);
  not not_6 (not_6_out, nand_2_out);
  nand nand_3 (nand_3_out, ADDR[15], ADDR[14], not_3_out, not_4_out);
  nor nor_1 (nor_1_out, nand_1_out, not_6_out);
  nor nor_2 (A12, nand_3_out, not_5_out);
  // Probe on nor_1_out
  // Probe on A12
  nor nor_3 (nCE, nor_1_out, A12);
  not not_7 (not_7_out, nCE);
  nand nand_4 (nand_4_out, not_7_out, not_1_out);
  not not_8 (not_8_out, nand_4_out);
  nand nand_5 (nWE, not_8_out, not_2_out);
  nand nand_6 (nOE, not_7_out, nWRAM);
endmodule
