// Logisim project extram_glue_logic.circ as structural Verilog: 1 circuit, main circuit main
module main (
  input  [15:0] ADDR,
  input  [7:0] DATA,
  input  n_WRAM,
  output [18:0] RAM_ADDR,
  output n_OEhi,
  output n_CEhi,
  output n_WEhi,
  output n_OElo,
  output n_CElo,
  output n_WElo
);

  wire ADDR_C2, clock_1_out, n74245_1_pin1, n74245_2_pin1, n_ADDR_C2, n_ADDR_D, n_ADDR_E, n_SEGD_RD,
       n_SEGD_SEL, n_SEGE_RD, n_SEGE_SEL, n_WE, nand_1_out, nand_2_out, nand_3_out, nand_6_out, not_1_out,
       not_5_out, not_6_out, pA19, WRAM;
  wire [7:0] SEGD, SEGE;

  Clock clock_1 (.out(clock_1_out));
  not not_1 (not_1_out, ADDR[0]);
  nand nand_1 (nand_1_out, ADDR[15], ADDR[14]);
  nand nand_2 (nand_2_out, ~ADDR[13], ADDR[12]);  // NAND_Gate
  nand nand_3 (nand_3_out, ADDR[13], ~ADDR[12]);  // NAND_Gate
  or or_1 (n_WE, clock_1_out, n_WRAM);
  not not_2 (WRAM, n_WRAM);
  or or_2 (n_SEGD_RD, n_SEGD_SEL, WRAM);
  or or_3 (n_SEGE_RD, WRAM, n_SEGE_SEL);
  _74245 u_74245_1 (
    .pin1(n74245_1_pin1), .pin2(DATA[7]), .pin3(DATA[6]), .pin4(DATA[5]), .pin5(DATA[4]), .pin6(DATA[3]),
    .pin7(DATA[2]), .pin8(DATA[1]), .pin9(DATA[0]), .pin19(n_SEGD_RD), .pin18(SEGD[7]), .pin17(SEGD[6]),
    .pin16(SEGD[5]), .pin15(SEGD[4]), .pin14(SEGD[3]), .pin13(SEGD[2]), .pin12(SEGD[1]), .pin11(SEGD[0]));
  nand nand_4 (n_SEGD_SEL, ADDR_C2, not_1_out);
  nand nand_5 (n_SEGE_SEL, ADDR_C2, ADDR[0]);
  or or_4 (n_ADDR_D, nand_1_out, nand_2_out);
  or or_5 (n_ADDR_E, nand_1_out, nand_3_out);
  nand nand_6 (nand_6_out, n_ADDR_D, n_ADDR_E);
  not not_3 (n_CEhi, nand_6_out);
  // Probe on DATA
  _74245 u_74245_2 (
    .pin1(n74245_2_pin1), .pin2(DATA[7]), .pin3(DATA[6]), .pin4(DATA[5]), .pin5(DATA[4]), .pin6(DATA[3]),
    .pin7(DATA[2]), .pin8(DATA[1]), .pin9(DATA[0]), .pin19(n_SEGE_RD), .pin18(SEGE[7]), .pin17(SEGE[6]),
    .pin16(SEGE[5]), .pin15(SEGE[4]), .pin14(SEGE[3]), .pin13(SEGE[2]), .pin12(SEGE[1]), .pin11(SEGE[0]));
  or or_6 (n_ADDR_C2, ADDR[8], ~ADDR[9], ADDR[10], ADDR[11], ADDR[12], ADDR[13], ~ADDR[14], ~ADDR[15]);  // OR_Gate
  not not_4 (ADDR_C2, n_ADDR_C2);
  or or_7 (n_WEhi, n_WE, ~pA19);  // OR_Gate
  or or_8 (n_WElo, n_WE, pA19);
  Register u_SEGD (.D(DATA), .en(not_5_out), .clk(n_WE), .Q(SEGD), .clr(1'b0));
  not not_5 (not_5_out, n_SEGD_SEL);
  Register u_SEGE (.D(DATA), .en(not_6_out), .clk(n_WE), .Q(SEGE), .clr(1'b0));
  not not_6 (not_6_out, n_SEGE_SEL);
  // Probe on SEGD
  // Probe on SEGE
  or or_9 (n_OEhi, WRAM, ~pA19);  // OR_Gate
  or or_10 (n_OElo, WRAM, pA19);
  Multiplexer #(.width(8)) multiplexer_1 (.in0(SEGD), .in1(SEGE), .out({pA19, RAM_ADDR[18:12]}), .sel(n_ADDR_D));

  assign n_CElo = n_CEhi;
  assign RAM_ADDR[11:0] = ADDR[11:0];
  // also tied to GND on the sheet: {n74245_1_pin1, n74245_2_pin1}

  // Other names for the same wires on the sheet: A12 = ADDR[12]; A13 = ADDR[13]; A14 = ADDR[14]; A15 = ADDR[15];
  //   n_ADDR_DE = n_CEhi; pA19_pA12[7:0] = {pA19, RAM_ADDR[18:12]}; A0 = ADDR[0]; ADDR_12bit[11:0] = ADDR[11:0]
endmodule
