// Logisim project interrupt_handler.circ as structural Verilog: 1 circuit, main circuit interrupt_handler
module interrupt_handler (
  input  IRQ7,
  input  IRQ6,
  input  IRQ5,
  input  IRQ4,
  input  IRQ3,
  input  IRQ2,
  input  IRQ1,
  input  IRQ0,
  input  MASK_INT,
  input  UNMASK_INT,
  output [7:0] PERIPH_BASE,
  output IRQOP
);

  wire CLK_out, ic_74112_1_p6, ic_74148_1_p9, not_1_out, not_2_out, RST_out;

  Button RST (.out(RST_out));
  Button CLK (.out(CLK_out));
  not not_1 (not_1_out, RST_out);
  not not_2 (not_2_out, CLK_out);
  // IC_74112 ic_74112_1: pin names not known; wires that end beside it: MASK_INT, not_2_out, UNMASK_INT, not_1_out, 1'b1, ic_74112_1_p6, IRQ2, IRQ1, IRQ0, ic_74112_1_p6
  // IC_74148 ic_74148_1: pin names not known; wires that end beside it: IRQ7, IRQ6, IRQ5, IRQ4, IRQ3, PERIPH_BASE[3], PERIPH_BASE[4], PERIPH_BASE[5], ic_74148_1_p9
  not not_3 (IRQOP, ic_74148_1_p9);

  assign {PERIPH_BASE[7:6], PERIPH_BASE[2:0]} = 5'b11000;
endmodule
