// Logisim project keyboard_controller.circ as structural Verilog: 1 circuit, main circuit main
module main (
  input  [15:0] ADDR,
  input  [7:0] DATA
);

  wire ADDR_KB, ADDRH_C0, ADDRL_KB, not_1_out, not_2_out, not_3_out, not_4_out;

  Button RST ();  // open: out
  not not_1 (not_1_out, ADDR[14]);
  not not_2 (not_2_out, ADDR[15]);
  nor nor_1 (ADDRL_KB, 1'b0, 1'b0, ADDR[2], ADDR[3], ADDR[4], ADDR[5], ADDR[6], ADDR[7]);
  nor nor_2 (ADDRH_C0, ADDR[8], ADDR[9], ADDR[10], ADDR[11], ADDR[12], ADDR[13], not_1_out, not_2_out);
  not not_3 (not_3_out, ADDRL_KB);
  not not_4 (not_4_out, ADDRH_C0);
  nor nor_3 (ADDR_KB, not_3_out, not_4_out);
endmodule
