// Logisim project keyboard_glue_logic.circ as structural Verilog: 1 circuit, main circuit main
module main (
  input  [15:0] ADDR,
  input  CPU_INT,
  input  RST,
  output n_FLAGS_OE,
  output n_KEY_OE,
  output n_IRQ1
);

  wire ADDR_KB, ADDRH_C0, CLK_out, n_A0, n_A7, n_ADDR_KB, n_ADDRH_C0, nand_1_out, nand_2_out, nand_3_out,
       not_1_out, not_2_out;

  Clock CLK (.out(CLK_out));
  not not_1 (not_1_out, ADDR[14]);
  not not_2 (not_2_out, ADDR[15]);
  nand nand_1 (nand_1_out, n_ADDR_KB, RST);
  or or_1 (n_ADDRH_C0, ADDR[8], ADDR[9], ADDR[10], ADDR[11], ADDR[12], ADDR[13], not_1_out, not_2_out);
  not not_3 (n_A0, ADDR[0]);
  not not_4 (n_A7, ADDR[7]);
  not not_5 (ADDRH_C0, n_ADDRH_C0);
  nand nand_2 (nand_2_out, nand_1_out, CLK_out);
  nand nand_3 (nand_3_out, CPU_INT, n_IRQ1);
  nand nand_4 (n_IRQ1, nand_3_out, nand_2_out);
  nand nand_5 (n_ADDR_KB, ADDRH_C0, n_A7);
  nand nand_6 (n_FLAGS_OE, ADDR_KB, ADDR[0]);
  nand nand_7 (n_KEY_OE, ADDR_KB, n_A0);
  not not_6 (ADDR_KB, n_ADDR_KB);

  // Other names for the same wires on the sheet: A0 = ADDR[0]; A7 = ADDR[7]
endmodule
