// Logisim project timer_control.circ as structural Verilog: 2 circuits, main circuit main
module main (
  input  [15:0] ADDR,
  input  n_WRAM,
  input  n_RST,
  input  CLK,
  output IRQ0
);

  wire and_1_out, and_2_out, and_4_out, bits_0123_p9, ic_74112_1_p4, ic_74112_1_p10, ic_74151_1_p10,
       ic_cd4020_1_q7, ic_cd4020_1_q8, ic_cd4020_1_q9, ic_cd4020_1_q10, ic_cd4020_1_q11, ic_cd4020_1_q12,
       ic_cd4020_1_q13, ic_cd4020_1_q14, n_RTC_ACT, n_TIMERCTL_ACT, n_TIMERCTL_OE, n_TIMERCTL_WRITE,
       not_1_out, not_2_out, not_3_out, not_6_out, not_7_out, RTC_ACT, SQW_out, TIMERCTL_ACT;
  wire [2:0] bits_0123_p6;
  wire [7:0] pull_resistor_1_node, undriven;

  // DipSwitch dipswitch_1: pin names not known
  not not_1 (not_1_out, ADDR[14]);
  not not_2 (not_2_out, ADDR[15]);
  not not_3 (not_3_out, n_WRAM);
  // Probe on undriven
  Pull_Resistor #(.pull(1)) pull_resistor_1 (.node(pull_resistor_1_node));
  assign pull_resistor_1_node = n_TIMERCTL_OE ? undriven : 8'bz;  // Controlled_Buffer controlled_buffer_1
  and and_1 (and_1_out, TIMERCTL_ACT, not_3_out);
  not not_4 (n_TIMERCTL_WRITE, and_1_out);
  and and_2 (and_2_out, TIMERCTL_ACT, n_WRAM);
  not not_5 (n_TIMERCTL_OE, and_2_out);
  // Probe on pull_resistor_1_node
  or or_1 (n_RTC_ACT, ADDR[8], ADDR[9], ADDR[10], ADDR[11], ADDR[12], ADDR[13], not_1_out, not_2_out);
  not not_6 (not_6_out, ADDR[8]);
  or or_2 (n_TIMERCTL_ACT, not_6_out, ADDR[9], ADDR[10], ADDR[11], ADDR[12], ADDR[13], not_1_out, not_2_out);
  not not_7 (not_7_out, n_RST);
  not not_8 (RTC_ACT, n_RTC_ACT);
  not not_9 (TIMERCTL_ACT, n_TIMERCTL_ACT);
  // IC_74173 bits_0123: pin names not known; wires that end beside it: pull_resistor_1_node[0], pull_resistor_1_node[1], pull_resistor_1_node[2], pull_resistor_1_node[3], CLK, bits_0123_p6[0], bits_0123_p6[1], bits_0123_p6[2], bits_0123_p9
  // IC_74112 ic_74112_1: pin names not known; wires that end beside it: n_TIMERCTL_WRITE, n_TIMERCTL_WRITE, not_7_out, ic_74112_1_p4, TIMERCTL_ACT, 1'b1, n_RST, 1'b0, 1'b0, ic_74112_1_p10, IRQ0
  // NOT_Gate not_10 has open pins: in=CLK, out=open
  // IC_74245 ic_74245_1: pin names not known; wires that end beside it: n_TIMERCTL_OE, ic_74112_1_p10, 1'b0, 1'b0, 1'b0, bits_0123_p9, bits_0123_p6[2], bits_0123_p6[1], bits_0123_p6[0]
  and and_3 (ic_74112_1_p4, bits_0123_p9, ic_74151_1_p10);
  and and_4 (and_4_out, IRQ0, bits_0123_p9);
  Clock SQW (.out(SQW_out));
  ic_cd4020 ic_cd4020_1 (
    .Q7(ic_cd4020_1_q7), .Q8(ic_cd4020_1_q8), .Q9(ic_cd4020_1_q9), .Q10(ic_cd4020_1_q10),
    .Q11(ic_cd4020_1_q11), .Q12(ic_cd4020_1_q12), .Q13(ic_cd4020_1_q13), .Q14(ic_cd4020_1_q14),
    .CLK(SQW_out), .n_RST(and_4_out));  // open: Q1, Q4, Q5, Q6
  // IC_74151 ic_74151_1: pin names not known; wires that end beside it: ic_cd4020_1_q7, ic_cd4020_1_q8, ic_cd4020_1_q9, ic_cd4020_1_q10, ic_cd4020_1_q11, ic_cd4020_1_q12, ic_cd4020_1_q13, ic_cd4020_1_q14, 1'b0, ic_74151_1_p10

  // Notes on the sheet:
  //   Timer Control Register
  //   bit 0-2: timer divisor
  //   bit 3: timer interrupt enable
  //   bit 7: timer interrupt
  //   74x4078 OR/NOR gates
  //   IRQ0
  //   timer irq enable
  //   2x 74x4078 8-input OR/NOR gates
  //   1x quad AND gate
  //   2x (maybe 1x?) hex inverter
  //   1x 74x173 quad D-FF
  //   1x 74x112 JK FF (use existing?)
  //   1x 74x245 bus transceiver
  //   1x CD4020 ripple counter
  //   1x 74x151 8:1 selector
  //   RTC chip
  //   timer irq enable
endmodule

module ic_cd4020 (
  input  n_RST,
  input  CLK,
  output Q1,
  output Q4,
  output Q5,
  output Q6,
  output Q7,
  output Q8,
  output Q9,
  output Q10,
  output Q11,
  output Q12,
  output Q13,
  output Q14
);

  wire not_1_out;
  wire [2:1] counter_1_q;

  Counter #(.max('h3fff), .width(14)) counter_1 (
    .clr(not_1_out), .load(1'b0), .up(1'b1), .count(1'b1), .clk(CLK),
    .Q({Q14, Q13, Q12, Q11, Q10, Q9, Q8, Q7, Q6, Q5, Q4, counter_1_q, Q1}));  // open: D, carry
  not not_1 (not_1_out, n_RST);
endmodule
