// Logisim project uart_glue_logic.circ as structural Verilog: 1 circuit, main circuit main
module main (
  input  [15:0] ADDR_BUS,
  input  n_WRAM,
  input  [3:0] SEQ,
  input  CPU_RST,
  input  INTR,
  input  DR,
  input  [7:0] DATA_BUS,
  output [1:0] ADDR,
  output n_CSO,
  output n_RD,
  output n_WR,
  output RST,
  output n_IRQ4,
  output n_IRQ5,
  output [7:0] DATA
);

  wire CLK_out, F26_27_out, n74377_1_pin1, n74377_1_pin13, n74377_1_pin14, n74377_1_pin16, n74377_1_pin17,
       nor_1_out, not_1_out, not_5_out, not_6_out;

  Clock CLK (.out(CLK_out));
  // NoConnect on ADDR_BUS[7:2]
  not not_1 (not_1_out, CLK_out);
  _74377 u_74377_1 (
    .pin1(n74377_1_pin1), .pin17(n74377_1_pin17), .pin16(n74377_1_pin16), .pin15(n_RD),
    .pin14(n74377_1_pin14), .pin13(n74377_1_pin13), .pin12(n_WR), .pin11(not_1_out));  // open: pin2, pin3, pin4, pin5, pin6, pin7, pin8, pin9, pin19, pin18
  nor nor_1 (nor_1_out, ~SEQ[0], SEQ[1], ~SEQ[2], SEQ[3]);  // NOR_Gate
  nor nor_2 (n74377_1_pin17, ~ADDR_BUS[15], ~ADDR_BUS[14], ADDR_BUS[13], ADDR_BUS[12], ADDR_BUS[11], ADDR_BUS[10], ADDR_BUS[9], ~ADDR_BUS[8]);  // NOR_Gate
  // Probe on n74377_1_pin17
  not not_2 (n_CSO, n74377_1_pin16);
  nand F26_27 (F26_27_out, n74377_1_pin16, nor_1_out);
  not not_3 (n_IRQ4, INTR);
  not not_4 (n_IRQ5, DR);
  not not_5 (not_5_out, F26_27_out);
  not not_6 (not_6_out, n_WRAM);
  nand F29_30 (n74377_1_pin14, n_WRAM, not_5_out);
  nand E28_29 (n74377_1_pin13, not_5_out, not_6_out);

  assign ADDR = ADDR_BUS[1:0];
  assign DATA = DATA_BUS;
  assign RST = CPU_RST;
  // also tied to GND on the sheet: n74377_1_pin1

  // Notes on the sheet:
  //   n_WRAM: initial=0x1
  //   SEQ: initial=0x1
  //   CPU_RST: initial=0x1
  //   DATA_BUS: initial=0xff
  //   ADDR_BUS: initial=0xffff
  //   /WRAM only during sequence 0x5
  //   Group C G-J
  //   Assumes read and write operations that hold the address
  //   Group E G-H
  //   and/or data bus stable across sequences 0x4-0x6, and assert
  //   7D
  //   7Q
  //   6Q
  //   6D
  //   5D
  //   5Q
  //   Group F E-F
  //   Group F E-F
endmodule
