// Logisim project main_memory.circ as structural Verilog: 1 circuit, main circuit main_memory
module main_memory (
  input  [15:0] AddrBusIn,
  input  OE_n,
  input  WE_n,
  input  CLK,
  input  [7:0] DataBusIn,
  output [7:0] DataBusOut
);

  wire and_1_out, not_1_out, not_2_out, not_3_out, OE_RAM, OE_ROM, WE_RAM;
  wire [7:0] AT28C256_data;

  not not_1 (not_1_out, OE_n);
  not not_2 (not_2_out, WE_n);
  RAM #(.addrWidth(15), .trigger("low")) AT28C256 (
    .addr(AddrBusIn[14:0]), .we(1'b1), .oe(OE_ROM), .data(AT28C256_data));
  RAM #(.addrWidth(15), .trigger("low")) IDT7007 (
    .addr(AddrBusIn[14:0]), .we(WE_RAM), .oe(OE_RAM), .data(AT28C256_data));
  or or_1 (OE_ROM, AddrBusIn[14], AddrBusIn[15], OE_n);
  nand nand_1 (OE_RAM, AddrBusIn[15], WE_n, not_1_out);
  nand nand_2 (WE_RAM, AddrBusIn[15], not_2_out, CLK);
  assign DataBusOut = not_3_out ? AT28C256_data : 8'bz;  // Controlled_Buffer controlled_buffer_1
  not not_3 (not_3_out, and_1_out);
  assign AT28C256_data = and_1_out ? DataBusIn : 8'bz;  // Controlled_Buffer controlled_buffer_2
  and and_1 (and_1_out, OE_RAM, OE_ROM);

  // Other names for the same wires on the sheet: InternalAddr[14:0] = AddrBusIn[14:0]

  // Notes on the sheet:
  //   0x0000 - 0x3FFF ROM
  //   0x4000 - 0x7FFF I/O
  //   0x8000 - 0xFFFF RAM
endmodule
