// Logisim project mycpu2.circ as structural Verilog: 2 circuits, main circuit mycpu
module mycpu (
);

  wire A_equal_B, ALU_OE_n, clock_1_out, control_unit_1_alu_oe_n, control_unit_1_imm_addr_oe_n,
       control_unit_1_imm_we_h_n, control_unit_1_imm_we_l_n, control_unit_1_ir_we_n,
       control_unit_1_irq_addr_oe_n, control_unit_1_irq_mask, control_unit_1_mem_oe_n,
       control_unit_1_mem_we_n, control_unit_1_pc_count, control_unit_1_pc_we_n, control_unit_1_ra_hilo_sel,
       control_unit_1_ra_input_sel, control_unit_1_ra_we_n, control_unit_1_rb_hilo_sel,
       control_unit_1_rb_input_sel, control_unit_1_rb_we_n, control_unit_1_sequence_rst_n,
       control_unit_1_sp_count_n, control_unit_1_sp_downup_n, control_unit_1_sp_oe_n,
       control_unit_1_status_we_n, dipswitch_1_sw2, IMM_ADDR_OE_n, IMM_WE_H_n, IMM_WE_L_n, INTERRUPT,
       interrupt_handler_1_interrupt_n, IR_WE_n, IRQ_ADDR_OE_n, IRQ_MASK, MEM_OE_n, MEM_WE_n, not_1_out,
       PC_COUNT, PC_WE_n, RA_HiLo_SEL, RA_INPUT_SEL, RA_WE_n, RB_HiLo_SEL, RB_INPUT_SEL, RB_WE_n,
       SEQUENCE_RST_n, SP_COUNT_n, SP_DOWNUP_n, SP_OE_n, STATUS_WE_n, ZERO;
  wire [1:0] control_unit_1_pc_output_sel, control_unit_1_ra_output_sel, control_unit_1_rb_output_sel,
       PC_OUTPUT_SEL, RA_OUTPUT_SEL, RB_OUTPUT_SEL;
  wire [3:0] SEQUENCE, undriven;
  wire [7:0] ALU_OP, ALUBUS_A, ALUBUS_B, INSTRUCTION, main_memory_1_databusout;
  wire [15:0] RegisterA_addrbusout;

  Clock clock_1 (.out(clock_1_out));
  DipSwitch #(.number(2)) dipswitch_1 (.sw2(dipswitch_1_sw2));  // open: sw1
  not not_1 (not_1_out, dipswitch_1_sw2);
  // Probe on RA_OUTPUT_SEL
  // Probe on RB_OUTPUT_SEL
  // Probe on PC_OUTPUT_SEL
  main_memory main_memory_1 (
    .AddrBusIn(RegisterA_addrbusout), .OE_n(MEM_OE_n), .WE_n(MEM_WE_n), .CLK(clock_1_out),
    .DataBusOut(main_memory_1_databusout), .DataBusIn(main_memory_1_databusout));
  register_pair RegisterA (
    .OUTPUT_SEL(RA_OUTPUT_SEL), .CLK(clock_1_out), .WE_n(RA_WE_n), .HiLo_SEL(RA_HiLo_SEL),
    .INPUT_SEL(RA_INPUT_SEL), .DataBusIn(main_memory_1_databusout), .AddrBusIn(RegisterA_addrbusout),
    .AddrBusOut(RegisterA_addrbusout), .DataBusOut(main_memory_1_databusout), .ALUBusOut(ALUBUS_A));
  register_pair RegisterB (
    .OUTPUT_SEL(RB_OUTPUT_SEL), .CLK(clock_1_out), .WE_n(RB_WE_n), .HiLo_SEL(RB_HiLo_SEL),
    .INPUT_SEL(RB_INPUT_SEL), .DataBusIn(main_memory_1_databusout), .AddrBusIn(RegisterA_addrbusout),
    .AddrBusOut(RegisterA_addrbusout), .DataBusOut(main_memory_1_databusout), .ALUBusOut(ALUBUS_B));
  program_counter program_counter_1 (
    .DataBusOut(main_memory_1_databusout), .OUTPUT_SEL(PC_OUTPUT_SEL), .WE_n(PC_WE_n),
    .AddrBusIn(RegisterA_addrbusout), .RST_n(not_1_out), .COUNT(PC_COUNT), .CLK(clock_1_out),
    .AddrBusOut(RegisterA_addrbusout));
  sequence_counter sequence_counter_1 (
    .SEQUENCE(SEQUENCE), .CLK(clock_1_out), .ASYNC_RST_n(not_1_out), .SYNC_RST_n(SEQUENCE_RST_n), .COUNT(1'b1));
  interrupt_handler interrupt_handler_1 (
    .IRQ_MASK(IRQ_MASK), .IRQ_7_n(1'b1), .IRQ_6_n(1'b1), .IRQ_5_n(1'b1), .IRQ_4_n(1'b1), .IRQ_3_n(1'b1),
    .IRQ_2_n(1'b1), .IRQ_1_n(1'b1), .IRQ_0_n(1'b1), .IRQ_ADDR_OE_n(IRQ_ADDR_OE_n),
    .IRQ_ADDR(RegisterA_addrbusout), .INTERRUPT_n(interrupt_handler_1_interrupt_n));
  stack_pointer stack_pointer_1 (
    .CLK(clock_1_out), .RST_n(not_1_out), .OE_n(SP_OE_n), .D_U(SP_DOWNUP_n), .COUNT_n(SP_COUNT_n),
    .AddrBusOut(RegisterA_addrbusout));
  instruction_register instruction_register_1 (
    .INSTRUCTION(INSTRUCTION), .CLK(clock_1_out), .RST_n(not_1_out), .WE_n(IR_WE_n),
    .DataBusIn(main_memory_1_databusout));
  // Probe on main_memory_1_databusout
  // Probe on SEQUENCE
  // Probe on INSTRUCTION
  immediate_register immediate_register_1 (
    .CLK(clock_1_out), .WE_L_n(IMM_WE_L_n), .DataBusIn(main_memory_1_databusout), .ALU_OP(ALU_OP),
    .WE_H_n(IMM_WE_H_n), .AddrBusOut(RegisterA_addrbusout), .ADDR_OE_n(IMM_ADDR_OE_n));
  not not_2 (INTERRUPT, interrupt_handler_1_interrupt_n);
  // Probe on RegisterA_addrbusout
  alu alu_1 (
    .RST_n(not_1_out), .ALU_OP(ALU_OP[5:0]), .OE_n(ALU_OE_n), .DataBusOut(main_memory_1_databusout),
    .WE_n(STATUS_WE_n), .A(ALUBUS_A), .B(ALUBUS_B), .CLK(clock_1_out), .A_equal_B(A_equal_B), .ZERO(ZERO));
  control_unit control_unit_1 (
    .Sequence(SEQUENCE), .Flags({INTERRUPT, ZERO, A_equal_B}), .Instruction(INSTRUCTION),
    .RA_OUTPUT_SEL(control_unit_1_ra_output_sel), .RA_WE_n(control_unit_1_ra_we_n),
    .RA_HiLo_SEL(control_unit_1_ra_hilo_sel), .RA_INPUT_SEL(control_unit_1_ra_input_sel),
    .MEM_OE_n(control_unit_1_mem_oe_n), .MEM_WE_n(control_unit_1_mem_we_n),
    .PC_COUNT(control_unit_1_pc_count), .RB_OUTPUT_SEL(control_unit_1_rb_output_sel),
    .RB_WE_n(control_unit_1_rb_we_n), .RB_HiLo_SEL(control_unit_1_rb_hilo_sel),
    .RB_INPUT_SEL(control_unit_1_rb_input_sel), .PC_WE_n(control_unit_1_pc_we_n),
    .PC_OUTPUT_SEL(control_unit_1_pc_output_sel), .SP_COUNT_n(control_unit_1_sp_count_n),
    .SP_DOWNUP_n(control_unit_1_sp_downup_n), .SP_OE_n(control_unit_1_sp_oe_n),
    .SEQUENCE_RST_n(control_unit_1_sequence_rst_n), .IR_WE_n(control_unit_1_ir_we_n),
    .IMM_WE_L_n(control_unit_1_imm_we_l_n), .IMM_WE_H_n(control_unit_1_imm_we_h_n),
    .IMM_ADDR_OE_n(control_unit_1_imm_addr_oe_n), .ALU_OE_n(control_unit_1_alu_oe_n),
    .STATUS_WE_n(control_unit_1_status_we_n), .IRQ_MASK(control_unit_1_irq_mask),
    .IRQ_ADDR_OE_n(control_unit_1_irq_addr_oe_n));
  assign RA_OUTPUT_SEL = 1'b0 ? control_unit_1_ra_output_sel : 2'bz;  // Controlled_Buffer controlled_buffer_1
  assign RA_WE_n = 1'b0 ? control_unit_1_ra_we_n : 1'bz;  // Controlled_Buffer controlled_buffer_2
  assign RA_HiLo_SEL = 1'b0 ? control_unit_1_ra_hilo_sel : 1'bz;  // Controlled_Buffer controlled_buffer_3
  assign RA_INPUT_SEL = 1'b0 ? control_unit_1_ra_input_sel : 1'bz;  // Controlled_Buffer controlled_buffer_4
  assign MEM_OE_n = 1'b0 ? control_unit_1_mem_oe_n : 1'bz;  // Controlled_Buffer controlled_buffer_5
  assign MEM_WE_n = 1'b0 ? control_unit_1_mem_we_n : 1'bz;  // Controlled_Buffer controlled_buffer_6
  assign PC_COUNT = 1'b0 ? control_unit_1_pc_count : 1'bz;  // Controlled_Buffer controlled_buffer_7
  assign RB_OUTPUT_SEL = 1'b0 ? control_unit_1_rb_output_sel : 2'bz;  // Controlled_Buffer controlled_buffer_8
  assign RB_WE_n = 1'b0 ? control_unit_1_rb_we_n : 1'bz;  // Controlled_Buffer controlled_buffer_9
  assign RB_HiLo_SEL = 1'b0 ? control_unit_1_rb_hilo_sel : 1'bz;  // Controlled_Buffer controlled_buffer_10
  assign RB_INPUT_SEL = 1'b0 ? control_unit_1_rb_input_sel : 1'bz;  // Controlled_Buffer controlled_buffer_11
  assign PC_WE_n = 1'b0 ? control_unit_1_pc_we_n : 1'bz;  // Controlled_Buffer controlled_buffer_12
  assign PC_OUTPUT_SEL = 1'b0 ? control_unit_1_pc_output_sel : 2'bz;  // Controlled_Buffer controlled_buffer_13
  assign SP_COUNT_n = 1'b0 ? control_unit_1_sp_count_n : 1'bz;  // Controlled_Buffer controlled_buffer_14
  assign SP_DOWNUP_n = 1'b0 ? control_unit_1_sp_downup_n : 1'bz;  // Controlled_Buffer controlled_buffer_15
  assign SP_OE_n = 1'b0 ? control_unit_1_sp_oe_n : 1'bz;  // Controlled_Buffer controlled_buffer_16
  assign SEQUENCE_RST_n = 1'b0 ? control_unit_1_sequence_rst_n : 1'bz;  // Controlled_Buffer controlled_buffer_17
  assign IR_WE_n = 1'b0 ? control_unit_1_ir_we_n : 1'bz;  // Controlled_Buffer controlled_buffer_18
  assign IMM_WE_L_n = 1'b0 ? control_unit_1_imm_we_l_n : 1'bz;  // Controlled_Buffer controlled_buffer_19
  assign IMM_WE_H_n = 1'b0 ? control_unit_1_imm_we_h_n : 1'bz;  // Controlled_Buffer controlled_buffer_20
  assign IMM_ADDR_OE_n = 1'b0 ? control_unit_1_imm_addr_oe_n : 1'bz;  // Controlled_Buffer controlled_buffer_21
  assign ALU_OE_n = 1'b0 ? control_unit_1_alu_oe_n : 1'bz;  // Controlled_Buffer controlled_buffer_22
  assign STATUS_WE_n = 1'b0 ? control_unit_1_status_we_n : 1'bz;  // Controlled_Buffer controlled_buffer_23
  assign IRQ_MASK = 1'b0 ? control_unit_1_irq_mask : 1'bz;  // Controlled_Buffer controlled_buffer_24
  assign IRQ_ADDR_OE_n = 1'b0 ? control_unit_1_irq_addr_oe_n : 1'bz;  // Controlled_Buffer controlled_buffer_25
  DipSwitch #(.number(32)) dipswitch_2 (
    .sw1(RA_OUTPUT_SEL[1]), .sw2(RA_OUTPUT_SEL[0]), .sw3(RA_WE_n), .sw4(RA_HiLo_SEL), .sw5(RA_INPUT_SEL),
    .sw6(MEM_OE_n), .sw7(MEM_WE_n), .sw8(PC_COUNT), .sw9(RB_OUTPUT_SEL[1]), .sw10(RB_OUTPUT_SEL[0]),
    .sw11(RB_WE_n), .sw12(RB_HiLo_SEL), .sw13(RB_INPUT_SEL), .sw14(PC_WE_n), .sw15(PC_OUTPUT_SEL[1]),
    .sw16(PC_OUTPUT_SEL[0]), .sw17(SP_COUNT_n), .sw18(SP_DOWNUP_n), .sw19(SP_OE_n), .sw20(SEQUENCE_RST_n),
    .sw21(IR_WE_n), .sw22(IMM_WE_L_n), .sw23(IMM_WE_H_n), .sw24(IMM_ADDR_OE_n), .sw25(ALU_OE_n),
    .sw26(STATUS_WE_n), .sw27(IRQ_MASK), .sw28(IRQ_ADDR_OE_n));  // open: sw29, sw30, sw31, sw32
  // Probe on {RA_OUTPUT_SEL[0], RA_OUTPUT_SEL[1], RA_WE_n, RA_HiLo_SEL, RA_INPUT_SEL, MEM_OE_n, MEM_WE_n, PC_COUNT}
  // Probe on {RB_OUTPUT_SEL[0], RB_OUTPUT_SEL[1], RB_WE_n, RB_HiLo_SEL, RB_INPUT_SEL, PC_WE_n, PC_OUTPUT_SEL[0], PC_OUTPUT_SEL[1]}
  // Probe on {SP_COUNT_n, SP_DOWNUP_n, SP_OE_n, SEQUENCE_RST_n, IR_WE_n, IMM_WE_L_n, IMM_WE_H_n, IMM_ADDR_OE_n}
  // Probe on {ALU_OE_n, STATUS_WE_n, IRQ_MASK, IRQ_ADDR_OE_n, undriven}
endmodule

module control_unit (
  input  [3:0] Sequence,
  input  [2:0] Flags,
  input  [7:0] Instruction,
  output [1:0] RA_OUTPUT_SEL,
  output RA_WE_n,
  output RA_HiLo_SEL,
  output RA_INPUT_SEL,
  output MEM_OE_n,
  output MEM_WE_n,
  output PC_COUNT,
  output [1:0] RB_OUTPUT_SEL,
  output RB_WE_n,
  output RB_HiLo_SEL,
  output RB_INPUT_SEL,
  output PC_WE_n,
  output [1:0] PC_OUTPUT_SEL,
  output SP_COUNT_n,
  output SP_DOWNUP_n,
  output SP_OE_n,
  output SEQUENCE_RST_n,
  output IR_WE_n,
  output IMM_WE_L_n,
  output IMM_WE_H_n,
  output IMM_ADDR_OE_n,
  output ALU_OE_n,
  output STATUS_WE_n,
  output IRQ_MASK,
  output IRQ_ADDR_OE_n
);

  wire [7:4] rom_4_data;

  ROM #(.addrWidth(15)) rom_1 (
    .addr({Instruction, Flags, Sequence}),
    .data({PC_COUNT, MEM_WE_n, MEM_OE_n, RA_INPUT_SEL, RA_HiLo_SEL, RA_WE_n, RA_OUTPUT_SEL}));
  ROM #(.addrWidth(15)) rom_2 (
    .addr({Instruction, Flags, Sequence}),
    .data({PC_OUTPUT_SEL, PC_WE_n, RB_INPUT_SEL, RB_HiLo_SEL, RB_WE_n, RB_OUTPUT_SEL}));
  ROM #(.addrWidth(15)) rom_3 (
    .addr({Instruction, Flags, Sequence}),
    .data({IMM_ADDR_OE_n, IMM_WE_H_n, IMM_WE_L_n, IR_WE_n, SEQUENCE_RST_n, SP_OE_n, SP_DOWNUP_n, SP_COUNT_n}));
  ROM #(.addrWidth(15)) rom_4 (
    .addr({Instruction, Flags, Sequence}), .data({rom_4_data, IRQ_ADDR_OE_n, IRQ_MASK, STATUS_WE_n, ALU_OE_n}));

  // Notes on the sheet:
  //   contents of rom_1 (hex, n*v repeats v):
  //   e4 15*0 e4
  //   contents of rom_2 (hex, n*v repeats v):
  //   c4 15*0 c4
  //   contents of rom_3 (hex, n*v repeats v):
  //   fd 15*0 fd
  //   contents of rom_4 (hex, n*v repeats v):
  //   b 15*0 b
endmodule
