// Logisim project program_counter.circ as structural Verilog: 1 circuit, main circuit program_counter
module program_counter (
  input  [15:0] AddrBusIn,
  input  WE_n,
  input  COUNT,
  input  RST_n,
  input  [1:0] OUTPUT_SEL,
  input  CLK,
  output [7:0] DataBusOut,
  output [15:0] AddrBusOut
);

  wire ic_74139_1_p4, ic_74139_1_p5, ic_74139_1_p6, ic_74161_1_p10, ic_74161_2_p10, ic_74161_3_p10;
  wire [7:0] ADDR_HI, ADDR_LO;

  // IC_74161 ic_74161_1: pin names not known; wires that end beside it: CLK, WE_n, COUNT, RST_n, COUNT, ADDR_LO[0], ADDR_LO[1], ADDR_LO[2], ADDR_LO[3], ic_74161_1_p10
  // IC_74161 ic_74161_2: pin names not known; wires that end beside it: CLK, WE_n, COUNT, RST_n, ic_74161_1_p10, ADDR_LO[4], ADDR_LO[5], ADDR_LO[6], ADDR_LO[7], ic_74161_2_p10
  // IC_74161 ic_74161_3: pin names not known; wires that end beside it: CLK, WE_n, COUNT, RST_n, ic_74161_2_p10, ADDR_HI[0], ADDR_HI[1], ADDR_HI[2], ADDR_HI[3], ic_74161_3_p10
  // IC_74161 ic_74161_4: pin names not known; wires that end beside it: CLK, WE_n, COUNT, RST_n, ic_74161_3_p10, ADDR_HI[4], ADDR_HI[5], ADDR_HI[6], ADDR_HI[7]
  // IC_74139 ic_74139_1: pin names not known; wires that end beside it: OUTPUT_SEL[0], OUTPUT_SEL[1], 1'b0, ic_74139_1_p4, ic_74139_1_p5, ic_74139_1_p6
  // IC_74245 ic_74245_1: pin names not known; wires that end beside it: ic_74139_1_p4
  // IC_74245 ic_74245_2: pin names not known; wires that end beside it: ic_74139_1_p5
  // IC_74245 ic_74245_3: pin names not known; wires that end beside it: ic_74139_1_p6
  // IC_74245 ic_74245_4: pin names not known; wires that end beside it: ic_74139_1_p6
endmodule
