// Logisim project register.circ as structural Verilog: 1 circuit, main circuit register_pair
module register_pair (
  input  [1:0] OUTPUT_SEL,
  input  WE_n,
  input  HiLo_SEL,
  input  INPUT_SEL,
  input  [7:0] DataBusIn,
  input  [15:0] AddrBusIn,
  input  CLK,
  output [15:0] AddrBusOut,
  output [7:0] DataBusOut,
  output [7:0] ALUBusOut
);

  wire and_1_out, ic_74139_1_p2, ic_74139_1_p3, ic_74139_1_p4, nand_1_out, nand_2_out, nand_3_out,
       nand_4_out, not_1_out, not_2_out, not_3_out, not_4_out, not_5_out, or_1_out, or_2_out;
  wire [7:0] ic_74157_1_p7, ic_74157_3_p12, ic_74377_1_p8, ic_74377_2_p15;

  not not_1 (not_1_out, WE_n);
  and and_1 (and_1_out, not_1_out, HiLo_SEL);
  not not_2 (not_2_out, and_1_out);
  or or_1 (or_1_out, WE_n, and_1_out);
  or or_2 (or_2_out, WE_n, not_2_out);
  // IC_74157 ic_74157_1: pin names not known; wires that end beside it: DataBusIn[0], AddrBusIn[0], DataBusIn[1], AddrBusIn[1], DataBusIn[2], INPUT_SEL, ic_74157_1_p7[0], ic_74157_1_p7[1], ic_74157_1_p7[2]
  // IC_74157 ic_74157_2: pin names not known; wires that end beside it: AddrBusIn[2], DataBusIn[3], AddrBusIn[3], DataBusIn[4], AddrBusIn[4], DataBusIn[5], AddrBusIn[5], DataBusIn[6], 1'b0, INPUT_SEL, ic_74157_1_p7[3], ic_74157_1_p7[4], ic_74157_1_p7[5], ic_74157_1_p7[6]
  // IC_74157 ic_74157_3: pin names not known; wires that end beside it: AddrBusIn[6], DataBusIn[7], AddrBusIn[7], DataBusIn[0], AddrBusIn[8], DataBusIn[1], AddrBusIn[9], DataBusIn[2], 1'b0, INPUT_SEL, ic_74157_1_p7[7], ic_74157_3_p12[0], ic_74157_3_p12[1], ic_74157_3_p12[2]
  // IC_74157 ic_74157_4: pin names not known; wires that end beside it: AddrBusIn[10], DataBusIn[3], AddrBusIn[11], DataBusIn[4], AddrBusIn[12], DataBusIn[5], AddrBusIn[13], DataBusIn[6], AddrBusIn[14], DataBusIn[7], AddrBusIn[15], 1'b0, INPUT_SEL, 1'b0, ic_74157_3_p12[3], ic_74157_3_p12[4], ic_74157_3_p12[5], ic_74157_3_p12[6], ic_74157_3_p12[7]
  // IC_74139 ic_74139_1: pin names not known; wires that end beside it: 1'b0, ic_74139_1_p2, ic_74139_1_p3, ic_74139_1_p4
  not not_3 (not_3_out, ic_74139_1_p2);
  not not_4 (not_4_out, ic_74139_1_p3);
  not not_5 (not_5_out, HiLo_SEL);
  // IC_74377 ic_74377_1: pin names not known; wires that end beside it: ic_74157_1_p7[0], ic_74157_1_p7[1], ic_74157_1_p7[2], ic_74157_1_p7[3], ic_74157_1_p7[4], ic_74157_1_p7[5], ic_74157_1_p7[6], ic_74377_1_p8[0], ic_74377_1_p8[1], ic_74377_1_p8[2], ic_74377_1_p8[3], ic_74377_1_p8[4], ic_74377_1_p8[5], ic_74377_1_p8[6]
  // IC_74377 ic_74377_2: pin names not known; wires that end beside it: ic_74157_1_p7[7], CLK, or_1_out, ic_74157_3_p12[0], ic_74157_3_p12[1], ic_74157_3_p12[2], ic_74157_3_p12[3], ic_74157_3_p12[4], ic_74157_3_p12[5], ic_74157_3_p12[6], ic_74157_3_p12[7], CLK, or_2_out, ic_74377_1_p8[7], ic_74377_2_p15[0], ic_74377_2_p15[1], ic_74377_2_p15[2], ic_74377_2_p15[3], ic_74377_2_p15[4], ic_74377_2_p15[5], ic_74377_2_p15[6], ic_74377_2_p15[7]
  nand nand_1 (nand_1_out, not_4_out, not_5_out);
  nand nand_2 (nand_2_out, not_4_out, HiLo_SEL);
  nand nand_3 (nand_3_out, not_3_out, not_5_out);
  nand nand_4 (nand_4_out, not_3_out, HiLo_SEL);
  // IC_74245 ic_74245_1: pin names not known; wires that end beside it: ic_74377_1_p8[0], ic_74377_1_p8[1], ic_74377_1_p8[2], ic_74377_1_p8[3], ic_74377_1_p8[4], ic_74377_1_p8[5], ic_74377_1_p8[6], AddrBusOut[0], AddrBusOut[1], AddrBusOut[2], AddrBusOut[3], AddrBusOut[4], AddrBusOut[5], AddrBusOut[6]
  // IC_74245 ic_74245_2: pin names not known; wires that end beside it: ic_74377_1_p8[7], ic_74139_1_p4, ic_74377_2_p15[0], ic_74377_2_p15[1], ic_74377_2_p15[2], ic_74377_2_p15[3], ic_74377_2_p15[4], ic_74377_2_p15[5], ic_74377_2_p15[6], AddrBusOut[7], AddrBusOut[8], AddrBusOut[9], AddrBusOut[10], AddrBusOut[11], AddrBusOut[12], AddrBusOut[13], AddrBusOut[14]
  // IC_74245 ic_74245_3: pin names not known; wires that end beside it: ic_74377_2_p15[7], ic_74139_1_p4, ic_74377_1_p8[0], ic_74377_1_p8[1], ic_74377_1_p8[2], ic_74377_1_p8[3], ic_74377_1_p8[4], ic_74377_1_p8[5], ic_74377_1_p8[6], AddrBusOut[15], DataBusOut[0], DataBusOut[1], DataBusOut[2], DataBusOut[3], DataBusOut[4], DataBusOut[5], DataBusOut[6]
  // IC_74245 ic_74245_4: pin names not known; wires that end beside it: ic_74377_1_p8[7], nand_1_out, ic_74377_2_p15[0], ic_74377_2_p15[1], ic_74377_2_p15[2], ic_74377_2_p15[3], ic_74377_2_p15[4], ic_74377_2_p15[5], ic_74377_2_p15[6], DataBusOut[7], DataBusOut[0], DataBusOut[1], DataBusOut[2], DataBusOut[3], DataBusOut[4], DataBusOut[5], DataBusOut[6]
  // IC_74245 ic_74245_5: pin names not known; wires that end beside it: ic_74377_2_p15[7], nand_2_out, ic_74377_1_p8[0], ic_74377_1_p8[1], ic_74377_1_p8[2], ic_74377_1_p8[3], ic_74377_1_p8[4], ic_74377_1_p8[5], ic_74377_1_p8[6], DataBusOut[7], ALUBusOut[0], ALUBusOut[1], ALUBusOut[2], ALUBusOut[3], ALUBusOut[4], ALUBusOut[5], ALUBusOut[6]
  // IC_74245 ic_74245_6: pin names not known; wires that end beside it: ic_74377_1_p8[7], nand_3_out, ic_74377_2_p15[0], ic_74377_2_p15[1], ic_74377_2_p15[2], ic_74377_2_p15[3], ic_74377_2_p15[4], ic_74377_2_p15[5], ic_74377_2_p15[6], ic_74377_2_p15[7], nand_4_out, ALUBusOut[7], ALUBusOut[0], ALUBusOut[1], ALUBusOut[2], ALUBusOut[3], ALUBusOut[4], ALUBusOut[5], ALUBusOut[6], ALUBusOut[7]

  // Notes on the sheet:
  //   LOW
  //   HIGH
  //   LOW
  //   HIGH
  //   LOW
  //   HIGH
  //   LOW
  //   HIGH
endmodule
