// Logisim project sequence_counter.circ as structural Verilog: 1 circuit, main circuit sequence_counter
module sequence_counter (
  input  COUNT,
  input  SYNC_RST_n,
  input  ASYNC_RST_n,
  input  CLK,
  output [3:0] SEQUENCE
);

  // IC_74161 ic_74161_1: pin names not known; wires that end beside it: CLK, SYNC_RST_n, COUNT, ASYNC_RST_n, COUNT
endmodule
