// Logisim project stack_pointer.circ as structural Verilog: 2 circuits, main circuit stack_pointer
module stack_pointer (
  input  COUNT_n,
  input  D_U,
  input  OE_n,
  input  RST_n,
  input  CLK,
  output [15:0] AddrBusOut
);

  wire and_1_out, ic_74x191_1_maxmin, ic_74x191_1_rco_n, ic_74x191_2_maxmin, ic_74x191_2_rco_n,
       ic_74x191_3_maxmin, or_1_out;
  wire [3:0] ic_74x191_1_count, ic_74x191_2_count, ic_74x191_3_count;

  IC_74x191 ic_74x191_1 (
    .COUNT(ic_74x191_1_count), .CLK(CLK), .LOAD_n(RST_n), .CTEN_n(COUNT_n), .D_U(D_U), .DATA(4'b0000),
    .RCO_n(ic_74x191_1_rco_n), .MAXMIN(ic_74x191_1_maxmin));
  IC_74x191 ic_74x191_2 (
    .COUNT(ic_74x191_2_count), .CLK(CLK), .LOAD_n(RST_n), .CTEN_n(ic_74x191_1_rco_n), .D_U(D_U),
    .DATA(4'b0000), .RCO_n(ic_74x191_2_rco_n), .MAXMIN(ic_74x191_2_maxmin));
  IC_74x191 ic_74x191_3 (
    .COUNT(ic_74x191_3_count), .CLK(CLK), .LOAD_n(RST_n), .CTEN_n(or_1_out), .D_U(D_U), .DATA(4'b0000),
    .MAXMIN(ic_74x191_3_maxmin));  // open: RCO_n
  or or_1 (or_1_out, ic_74x191_2_rco_n, ic_74x191_1_rco_n);
  and and_1 (and_1_out, ic_74x191_1_maxmin, ic_74x191_2_maxmin, ic_74x191_3_maxmin, ic_74x191_1_count[0]);
  // IC_74245 ic_74245_1: pin names not known; wires that end beside it: ic_74x191_1_count[0], ic_74x191_1_count[1], ic_74x191_1_count[2], ic_74x191_1_count[3], ic_74x191_2_count[0], ic_74x191_2_count[1], ic_74x191_2_count[2], ic_74x191_2_count[3], OE_n, AddrBusOut[0], AddrBusOut[1], AddrBusOut[2], AddrBusOut[3], AddrBusOut[4], AddrBusOut[5], AddrBusOut[6], AddrBusOut[7]
  // IC_74245 ic_74245_2: pin names not known; wires that end beside it: OE_n, AddrBusOut[8], AddrBusOut[9], AddrBusOut[10], AddrBusOut[11], AddrBusOut[12], AddrBusOut[13], AddrBusOut[14], AddrBusOut[15]
  LED StackOverflow (.in(and_1_out));
endmodule

module IC_74x191 (
  input  CTEN_n,
  input  D_U,
  input  LOAD_n,
  input  [3:0] DATA,
  input  CLK,
  output RCO_n,
  output [3:0] COUNT,
  output MAXMIN
);

  wire and_1_out, counter_1_carry, nor_1_out, not_1_out, not_2_out, not_3_out;

  not not_1 (not_1_out, CTEN_n);
  not not_2 (not_2_out, D_U);
  not not_3 (not_3_out, LOAD_n);
  Counter #(.width(4), .max('hf)) counter_1 (
    .clr(1'b0), .load(not_3_out), .up(not_2_out), .count(not_1_out), .clk(CLK), .D(DATA),
    .carry(counter_1_carry), .Q(COUNT));
  not not_4 (RCO_n, counter_1_carry);
  and and_1 (and_1_out, COUNT[0], COUNT[1], COUNT[2], COUNT[3]);
  or or_1 (MAXMIN, and_1_out, nor_1_out);
  nor nor_1 (nor_1_out, COUNT[0], COUNT[1], COUNT[2], COUNT[3]);
endmodule
